// Logisim project 8bit_CPU_attempt1.circ as structural Verilog: 7 circuits, main circuit ALU
module ALU (
  input  [7:0] A,
  input  [7:0] B,
  input  [2:0] ALU_Control,
  output [7:0] O,
  output Z_Flag,
  output C_Flag
);

  wire adder_1_cout, subtractor_1_bout;
  wire [7:0] adder_1_out, and_1_out, not_1_out, or_1_out, shifter_1_out, shifter_2_out, subtractor_1_out,
       xor_1_out;

  Multiplexer #(.select(3)) multiplexer_1 (
    .in0(1'b0), .in1(1'b0), .in2(1'b0), .in3(1'b0), .in4(1'b0), .in5(1'b0), .in6(subtractor_1_bout),
    .in7(adder_1_cout), .out(C_Flag), .sel(ALU_Control));
  Adder adder_1 (.a(A), .b(B), .out(adder_1_out), .cin(1'b0), .cout(adder_1_cout));
  Subtractor subtractor_1 (.a(A), .b(B), .out(subtractor_1_out), .bin(1'b0), .bout(subtractor_1_bout));
  assign and_1_out = A & B;  // AND_Gate and_1, 8 bits wide
  assign or_1_out = A | B;  // OR_Gate or_1, 8 bits wide
  assign xor_1_out = A ^ B;  // XOR_Gate xor_1, 8 bits wide
  assign not_1_out = ~A;  // NOT_Gate not_1, 8 bits wide
  Shifter shifter_1 (.in(A), .\dist (3'b001), .out(shifter_1_out));
  Shifter #(.shift("lr")) shifter_2 (.in(A), .\dist (3'b001), .out(shifter_2_out));
  Multiplexer #(.select(3), .width(8)) multiplexer_2 (
    .in0(adder_1_out), .in1(subtractor_1_out), .in2(and_1_out), .in3(or_1_out), .in4(xor_1_out),
    .in5(not_1_out), .in6(shifter_1_out), .in7(shifter_2_out), .out(O), .sel(ALU_Control));
  Comparator comparator_1 (.a(O), .b({8{1'b0}}), .eq(Z_Flag));  // open: gt, lt

  // Other names for the same wires on the sheet: ALU_Ctrl[2:0] = ALU_Control
endmodule

module Register_File (
  input  Write_En,
  input  [1:0] Read_Addr_A,
  input  [1:0] Write_Addr,
  input  [7:0] Data_In,
  input  CLK,
  input  Reset,
  input  [1:0] Read_Addr_B,
  output [7:0] Out_A,
  output [7:0] Out_B
);

  wire demultiplexer_1_out0, demultiplexer_1_out1, demultiplexer_1_out2, demultiplexer_1_out3;
  wire [7:0] R0_q, R1_q, R2_q, R3_q;

  Demultiplexer #(.select(2)) demultiplexer_1 (
    .out0(demultiplexer_1_out0), .out1(demultiplexer_1_out1), .out2(demultiplexer_1_out2),
    .out3(demultiplexer_1_out3), .in(Write_En), .sel(Write_Addr));
  Register R0 (.D(Data_In), .en(demultiplexer_1_out0), .Q(R0_q), .clk(CLK), .clr(Reset));
  Register R1 (.D(Data_In), .en(demultiplexer_1_out1), .Q(R1_q), .clk(CLK), .clr(Reset));
  Register R2 (.D(Data_In), .en(demultiplexer_1_out2), .Q(R2_q), .clk(CLK), .clr(Reset));
  Register R3 (.D(Data_In), .en(demultiplexer_1_out3), .Q(R3_q), .clk(CLK), .clr(Reset));
  Multiplexer #(.select(2), .width(8)) multiplexer_1 (
    .in0(R0_q), .in1(R1_q), .in2(R2_q), .in3(R3_q), .out(Out_A), .sel(Read_Addr_A));
  Multiplexer #(.select(2), .width(8)) multiplexer_2 (
    .in0(R0_q), .in1(R1_q), .in2(R2_q), .in3(R3_q), .out(Out_B), .sel(Read_Addr_B));
endmodule

module Program_Counter (
  input  [7:0] Jump_Addr,
  input  CLK,
  input  Reset,
  input  Jump_En,
  output [7:0] PC_Out
);

  wire [7:0] adder_1_out, multiplexer_1_out;

  Register register_1 (.D(multiplexer_1_out), .en(1'b1), .Q(PC_Out), .clk(CLK), .clr(Reset));
  Adder adder_1 (.a(PC_Out), .b(8'h1), .out(adder_1_out));  // open: cin, cout
  Multiplexer #(.width(8)) multiplexer_1 (.in0(adder_1_out), .in1(Jump_Addr), .out(multiplexer_1_out), .sel(Jump_En));
endmodule

module CPU (
  input  Reset
);

  wire CLK_out, control_unit_1_jump_en, control_unit_1_ram_we;
  wire [1:0] alu_1_z_flag, control_unit_1_mux_sel, register_1_q, rom_1_data, rom_1_data_2, rom_1_data_3,
       rom_1_data_4;
  wire [2:0] rom_1_data_5;
  wire [7:0] alu_1_o, multiplexer_1_out, program_counter_1_pc_out, ram_1_dout, register_file_1_out_a,
       register_file_1_out_b;
  wire [15:11] rom_1_data_6;

  Clock CLK (.out(CLK_out));
  ROM #(.dataWidth(16)) rom_1 (
    .addr(program_counter_1_pc_out),
    .data({rom_1_data_6, rom_1_data_5, rom_1_data_4, rom_1_data_3, rom_1_data_2, rom_1_data}));
  Program_Counter program_counter_1 (
    .Jump_Addr({rom_1_data_4, rom_1_data_3, rom_1_data_2, rom_1_data}), .CLK(CLK_out), .Reset(Reset),
    .Jump_En(control_unit_1_jump_en), .PC_Out(program_counter_1_pc_out));
  Multiplexer #(.select(2), .width(8)) multiplexer_1 (
    .in0(alu_1_o), .in1(ram_1_dout), .in2({rom_1_data_4, rom_1_data_3, rom_1_data_2, rom_1_data}),
    .out(multiplexer_1_out), .sel(control_unit_1_mux_sel));  // open: in3
  Control_Unit control_unit_1 (
    .Flags_in(register_1_q), .Opcode(rom_1_data_6[15:12]), .Jump_En(control_unit_1_jump_en),
    .RAM_WE(control_unit_1_ram_we), .MUX_Sel(control_unit_1_mux_sel));
  Register_File register_file_1 (
    .Write_En(rom_1_data_6[11]), .Read_Addr_A(rom_1_data_3), .Write_Addr(rom_1_data_4),
    .Data_In(multiplexer_1_out), .CLK(CLK_out), .Reset(Reset), .Read_Addr_B(rom_1_data_2),
    .Out_A(register_file_1_out_a), .Out_B(register_file_1_out_b));
  RAM ram_1 (
    .addr(register_file_1_out_b), .we(control_unit_1_ram_we), .oe(1'b1), .clk(CLK_out),
    .din(register_file_1_out_a), .dout(ram_1_dout));
  ALU alu_1 (
    .A(register_file_1_out_a), .B(register_file_1_out_b), .ALU_Control(rom_1_data_5), .O(alu_1_o),
    .Z_Flag(alu_1_z_flag[0]), .C_Flag(alu_1_z_flag[1]));
  Register #(.width(2)) register_1 (.D(alu_1_z_flag), .en(1'b1), .Q(register_1_q), .clk(CLK_out), .clr(Reset));

  // Notes on the sheet:
  //   contents of rom_1 (hex, n*v repeats v):
  //   804 8000
endmodule

module Control_Unit (
  input  [1:0] Flags_in,
  input  [3:0] Opcode,
  output Jump_En,
  output RAM_WE,
  output [1:0] MUX_Sel
);

  wire and_1_out, and_2_out, decoder_1_out6, decoder_1_out7, decoder_1_out8;

  Decoder #(.select(4)) decoder_1 (
    .out6(decoder_1_out6), .out7(decoder_1_out7), .out8(decoder_1_out8), .out9(RAM_WE), .out10(MUX_Sel[0]),
    .out11(MUX_Sel[1]), .sel(Opcode), .en(1'b1));  // open: out0, out1, out2, out3, out4, out5, out12, out13, out14, out15
  and and_1 (and_1_out, Flags_in[1], decoder_1_out6);
  and and_2 (and_2_out, Flags_in[0], decoder_1_out7);
  or or_1 (Jump_En, and_1_out, and_2_out, decoder_1_out8);
endmodule

module CPU_all (
  input  in_1
);

  wire adder_2_cout, and_1_out, and_2_out, clock_1_out, decoder_1_out6, decoder_1_out7, decoder_1_out8,
       decoder_1_out9, demultiplexer_1_out0, demultiplexer_1_out1, demultiplexer_1_out2,
       demultiplexer_1_out3, or_1_out, subtractor_1_bout;
  wire [1:0] comparator_1_eq, decoder_1_out10, ROM_1_data, ROM_1_data_3;
  wire [7:0] adder_1_out, adder_2_out, and_3_out, multiplexer_1_out, multiplexer_2_out, multiplexer_3_out,
       multiplexer_5_out, multiplexer_6_out, not_1_out, or_2_out, R0_q, R1_q, R2_q, R3_q, RAM_1_dout,
       register_1_q, shifter_1_out, shifter_2_out, subtractor_1_out, xor_1_out;
  wire [15:2] ROM_1_data_2;

  Decoder #(.select(4)) decoder_1 (
    .out6(decoder_1_out6), .out7(decoder_1_out7), .out8(decoder_1_out8), .out9(decoder_1_out9),
    .out10(decoder_1_out10[0]), .out11(decoder_1_out10[1]), .sel(ROM_1_data_2[15:12]), .en(1'b1));  // open: out0, out1, out2, out3, out4, out5, out12, out13, out14, out15
  Clock clock_1 (.out(clock_1_out));
  ROM #(.dataWidth(16)) ROM_1 (
    .addr(register_1_q), .data({ROM_1_data_2[15:6], ROM_1_data_3, ROM_1_data_2[3:2], ROM_1_data}));
  Register register_1 (.D(multiplexer_1_out), .en(1'b1), .Q(register_1_q), .clk(clock_1_out), .clr(in_1));
  Adder adder_1 (.a(register_1_q), .b(8'h1), .out(adder_1_out));  // open: cin, cout
  and and_1 (and_1_out, decoder_1_out6, comparator_1_eq[0]);
  and and_2 (and_2_out, decoder_1_out7, comparator_1_eq[0]);
  or or_1 (or_1_out, and_1_out, decoder_1_out8, and_2_out);
  Multiplexer #(.width(8)) multiplexer_1 (
    .in0(adder_1_out), .in1({ROM_1_data_2[7:6], ROM_1_data_3, ROM_1_data_2[3:2], ROM_1_data}),
    .out(multiplexer_1_out), .sel(or_1_out));
  Demultiplexer #(.select(2)) demultiplexer_1 (
    .out0(demultiplexer_1_out0), .out1(demultiplexer_1_out1), .out2(demultiplexer_1_out2),
    .out3(demultiplexer_1_out3), .in(ROM_1_data_2[11]), .sel(ROM_1_data_2[7:6]));
  Register R0 (.D(multiplexer_6_out), .en(demultiplexer_1_out0), .Q(R0_q), .clk(clock_1_out), .clr(in_1));
  Register R1 (.D(multiplexer_6_out), .en(demultiplexer_1_out1), .Q(R1_q), .clk(clock_1_out), .clr(in_1));
  Register R2 (.D(multiplexer_6_out), .en(demultiplexer_1_out2), .Q(R2_q), .clk(clock_1_out), .clr(in_1));
  Register R3 (.D(multiplexer_6_out), .en(demultiplexer_1_out3), .Q(R3_q), .clk(clock_1_out), .clr(in_1));
  Multiplexer #(.select(2), .width(8)) multiplexer_2 (
    .in0(R0_q), .in1(R1_q), .in2(R2_q), .in3(R3_q), .out(multiplexer_2_out), .sel(ROM_1_data_3));
  Multiplexer #(.select(2), .width(8)) multiplexer_3 (
    .in0(R0_q), .in1(R1_q), .in2(R2_q), .in3(R3_q), .out(multiplexer_3_out), .sel(ROM_1_data_2[3:2]));
  Multiplexer #(.select(3)) multiplexer_4 (
    .in0(1'b0), .in1(1'b0), .in2(1'b0), .in3(1'b0), .in4(1'b0), .in5(1'b0), .in6(subtractor_1_bout),
    .in7(adder_2_cout), .out(comparator_1_eq[1]), .sel(ROM_1_data_2[10:8]));
  RAM RAM_1 (
    .addr(multiplexer_3_out), .we(decoder_1_out9), .oe(1'b1), .clk(clock_1_out), .din(multiplexer_2_out),
    .dout(RAM_1_dout));
  Adder adder_2 (.a(multiplexer_2_out), .b(multiplexer_3_out), .out(adder_2_out), .cin(1'b0), .cout(adder_2_cout));
  Subtractor subtractor_1 (
    .a(multiplexer_2_out), .b(multiplexer_3_out), .out(subtractor_1_out), .bin(1'b0), .bout(subtractor_1_bout));
  assign and_3_out = multiplexer_2_out & multiplexer_3_out;  // AND_Gate and_3, 8 bits wide
  assign or_2_out = multiplexer_2_out | multiplexer_3_out;  // OR_Gate or_2, 8 bits wide
  assign xor_1_out = multiplexer_2_out ^ multiplexer_3_out;  // XOR_Gate xor_1, 8 bits wide
  assign not_1_out = ~multiplexer_2_out;  // NOT_Gate not_1, 8 bits wide
  Shifter shifter_1 (.in(multiplexer_2_out), .\dist (3'b001), .out(shifter_1_out));
  Shifter #(.shift("lr")) shifter_2 (.in(multiplexer_2_out), .\dist (3'b001), .out(shifter_2_out));
  Multiplexer #(.select(3), .width(8)) multiplexer_5 (
    .in0(adder_2_out), .in1(subtractor_1_out), .in2(and_3_out), .in3(or_2_out), .in4(xor_1_out),
    .in5(not_1_out), .in6(shifter_1_out), .in7(shifter_2_out), .out(multiplexer_5_out),
    .sel(ROM_1_data_2[10:8]));
  Comparator comparator_1 (.a(multiplexer_5_out), .b({8{1'b0}}), .eq(comparator_1_eq[0]));  // open: gt, lt
  Multiplexer #(.select(2), .width(8)) multiplexer_6 (
    .in0(multiplexer_5_out), .in1(RAM_1_dout),
    .in2({ROM_1_data_2[7:6], ROM_1_data_3, ROM_1_data_2[3:2], ROM_1_data}), .out(multiplexer_6_out),
    .sel(decoder_1_out10));  // open: in3
  Register #(.width(2)) register_2 (.D(comparator_1_eq), .en(1'b1), .clk(clock_1_out), .clr(in_1));  // open: Q

  // Notes on the sheet:
  //   C
  //   Z
endmodule

module CPU_peripherals (
  input  in_1
);

  wire adder_2_cout, and_1_out, and_2_out, clock_1_out, decoder_1_out6, decoder_1_out7, decoder_1_out8,
       decoder_1_out9, decoder_2_out0, decoder_2_out1, decoder_2_out2, decoder_2_out3, decoder_2_out4,
       decoder_2_out5, decoder_2_out6, decoder_2_out7, demultiplexer_1_out0, demultiplexer_1_out1,
       demultiplexer_1_out2, demultiplexer_1_out3, demultiplexer_2_out0, demultiplexer_2_out1, or_1_out,
       subtractor_1_bout;
  wire [1:0] comparator_1_eq, decoder_1_out10;
  wire [3:0] button_4_out;
  wire [7:0] adder_1_out, adder_2_out, and_3_out, multiplexer_1_out, multiplexer_2_out, multiplexer_3_out,
       multiplexer_5_out, multiplexer_6_out, multiplexer_7_out, not_1_out, or_2_out, R0_q, R1_q, R2_q, R3_q,
       RAM_1_dout, register_1_q, register_3_q, register_4_q, register_5_q, register_6_q, register_7_q,
       register_8_q, register_9_q, register_10_q, shifter_1_out, shifter_2_out, subtractor_1_out, xor_1_out;
  wire [15:0] ROM_1_data;

  Decoder #(.select(4)) decoder_1 (
    .out6(decoder_1_out6), .out7(decoder_1_out7), .out8(decoder_1_out8), .out9(decoder_1_out9),
    .out10(decoder_1_out10[0]), .out11(decoder_1_out10[1]), .sel(ROM_1_data[15:12]), .en(1'b1));  // open: out0, out1, out2, out3, out4, out5, out12, out13, out14, out15
  Clock clock_1 (.out(clock_1_out));
  ROM #(.dataWidth(16)) ROM_1 (.addr(register_1_q), .data(ROM_1_data));
  Register register_1 (.D(multiplexer_1_out), .en(1'b1), .Q(register_1_q), .clk(clock_1_out), .clr(in_1));
  Adder adder_1 (.a(register_1_q), .b(8'h1), .out(adder_1_out));  // open: cin, cout
  and and_1 (and_1_out, decoder_1_out6, comparator_1_eq[0]);
  and and_2 (and_2_out, decoder_1_out7, comparator_1_eq[0]);
  or or_1 (or_1_out, and_1_out, decoder_1_out8, and_2_out);
  Multiplexer #(.width(8)) multiplexer_1 (
    .in0(adder_1_out), .in1(ROM_1_data[7:0]), .out(multiplexer_1_out), .sel(or_1_out));
  Demultiplexer #(.select(2)) demultiplexer_1 (
    .out0(demultiplexer_1_out0), .out1(demultiplexer_1_out1), .out2(demultiplexer_1_out2),
    .out3(demultiplexer_1_out3), .in(ROM_1_data[11]), .sel(ROM_1_data[7:6]));
  Register R0 (.D(multiplexer_7_out), .en(demultiplexer_1_out0), .Q(R0_q), .clk(clock_1_out), .clr(in_1));
  Register R1 (.D(multiplexer_7_out), .en(demultiplexer_1_out1), .Q(R1_q), .clk(clock_1_out), .clr(in_1));
  Register R2 (.D(multiplexer_7_out), .en(demultiplexer_1_out2), .Q(R2_q), .clk(clock_1_out), .clr(in_1));
  Register R3 (.D(multiplexer_7_out), .en(demultiplexer_1_out3), .Q(R3_q), .clk(clock_1_out), .clr(in_1));
  Multiplexer #(.select(2), .width(8)) multiplexer_2 (
    .in0(R0_q), .in1(R1_q), .in2(R2_q), .in3(R3_q), .out(multiplexer_2_out), .sel(ROM_1_data[5:4]));
  Multiplexer #(.select(2), .width(8)) multiplexer_3 (
    .in0(R0_q), .in1(R1_q), .in2(R2_q), .in3(R3_q), .out(multiplexer_3_out), .sel(ROM_1_data[3:2]));
  Multiplexer #(.select(3)) multiplexer_4 (
    .in0(1'b0), .in1(1'b0), .in2(1'b0), .in3(1'b0), .in4(1'b0), .in5(1'b0), .in6(subtractor_1_bout),
    .in7(adder_2_cout), .out(comparator_1_eq[1]), .sel(ROM_1_data[10:8]));
  Demultiplexer demultiplexer_2 (
    .out0(demultiplexer_2_out0), .out1(demultiplexer_2_out1), .in(decoder_1_out9), .sel(multiplexer_3_out[7]));
  Adder adder_2 (.a(multiplexer_2_out), .b(multiplexer_3_out), .out(adder_2_out), .cin(1'b0), .cout(adder_2_cout));
  Subtractor subtractor_1 (
    .a(multiplexer_2_out), .b(multiplexer_3_out), .out(subtractor_1_out), .bin(1'b0), .bout(subtractor_1_bout));
  assign and_3_out = multiplexer_2_out & multiplexer_3_out;  // AND_Gate and_3, 8 bits wide
  assign or_2_out = multiplexer_2_out | multiplexer_3_out;  // OR_Gate or_2, 8 bits wide
  assign xor_1_out = multiplexer_2_out ^ multiplexer_3_out;  // XOR_Gate xor_1, 8 bits wide
  assign not_1_out = ~multiplexer_2_out;  // NOT_Gate not_1, 8 bits wide
  Shifter shifter_1 (.in(multiplexer_2_out), .\dist (3'b001), .out(shifter_1_out));
  Shifter #(.shift("lr")) shifter_2 (.in(multiplexer_2_out), .\dist (3'b001), .out(shifter_2_out));
  RAM RAM_1 (
    .addr(multiplexer_3_out), .we(demultiplexer_2_out0), .oe(1'b1), .clk(clock_1_out),
    .din(multiplexer_2_out), .dout(RAM_1_dout));
  Multiplexer #(.select(3), .width(8)) multiplexer_5 (
    .in0(adder_2_out), .in1(subtractor_1_out), .in2(and_3_out), .in3(or_2_out), .in4(xor_1_out),
    .in5(not_1_out), .in6(shifter_1_out), .in7(shifter_2_out), .out(multiplexer_5_out), .sel(ROM_1_data[10:8]));
  Comparator comparator_1 (.a(multiplexer_5_out), .b({8{1'b0}}), .eq(comparator_1_eq[0]));  // open: gt, lt
  Multiplexer #(.width(8)) multiplexer_6 (
    .in0(RAM_1_dout), .in1({4'b0000, button_4_out}), .out(multiplexer_6_out), .sel(multiplexer_3_out[7]));
  Multiplexer #(.select(2), .width(8)) multiplexer_7 (
    .in0(multiplexer_5_out), .in1(multiplexer_6_out), .in2(ROM_1_data[7:0]), .out(multiplexer_7_out),
    .sel(decoder_1_out10));  // open: in3
  Register #(.width(2)) register_2 (.D(comparator_1_eq), .en(1'b1), .clk(clock_1_out), .clr(in_1));  // open: Q
  Button button_1 (.out(button_4_out[3]));
  Decoder #(.select(3)) decoder_2 (
    .out0(decoder_2_out0), .out1(decoder_2_out1), .out2(decoder_2_out2), .out3(decoder_2_out3),
    .out4(decoder_2_out4), .out5(decoder_2_out5), .out6(decoder_2_out6), .out7(decoder_2_out7),
    .sel(multiplexer_3_out[2:0]), .en(demultiplexer_2_out1));
  Button button_2 (.out(button_4_out[2]));
  Button button_3 (.out(button_4_out[1]));
  Button button_4 (.out(button_4_out[0]));
  Register register_3 (.D(multiplexer_2_out), .en(decoder_2_out0), .Q(register_3_q), .clk(clock_1_out), .clr(in_1));
  Register register_4 (.D(multiplexer_2_out), .en(decoder_2_out1), .Q(register_4_q), .clk(clock_1_out), .clr(in_1));
  Register register_5 (.D(multiplexer_2_out), .en(decoder_2_out2), .Q(register_5_q), .clk(clock_1_out), .clr(in_1));
  Register register_6 (.D(multiplexer_2_out), .en(decoder_2_out3), .Q(register_6_q), .clk(clock_1_out), .clr(in_1));
  Register register_7 (.D(multiplexer_2_out), .en(decoder_2_out4), .Q(register_7_q), .clk(clock_1_out), .clr(in_1));
  Register register_8 (.D(multiplexer_2_out), .en(decoder_2_out5), .Q(register_8_q), .clk(clock_1_out), .clr(in_1));
  Register register_9 (.D(multiplexer_2_out), .en(decoder_2_out6), .Q(register_9_q), .clk(clock_1_out), .clr(in_1));
  Register register_10 (.D(multiplexer_2_out), .en(decoder_2_out7), .Q(register_10_q), .clk(clock_1_out), .clr(in_1));
  DotMatrix #(.inputtype("row"), .matrixcols(8), .matrixrows(8)) dotmatrix_1 (
    .row0(register_3_q), .row1(register_4_q), .row2(register_5_q), .row3(register_6_q), .row4(register_7_q),
    .row5(register_8_q), .row6(register_9_q), .row7(register_10_q));

  // Notes on the sheet:
  //   contents of ROM_1 (hex, n*v repeats v):
  //   b843 b800 b80 9018 b848 b801 b80 9018 b800 b80 a808 b880 888 b800 9008 b890 a848 b801 a10 701d b800
  //   b80 a8c8 b801 930 bc0 b807 a30 9008 b802 a10 702a b800 b80 a8c8 b801 830 bc0 b807 a30 9008 b804 a10
  //   7037 b801 b80 a8c8 e30 7034 9008 8037 b801 9008 b808 a10 7046 b801 b80 a8c8 f30 7042 9008 8046 b840
  //   814 9008 b801 b80 a8c8 b800 b80 a808 b880 888 9038 8008
  //   C
  //   Z
  //   p2_d
  //   p2_up
  //   p1_d
  //   VRAM
  //   p1_up
endmodule
